# Fritzing sketch GY-61 ADXL33 (saved by Fritzing 0.9.3b)

parts:
  元件1 = Arduino Uno (Rev3) - ICSP
  元件2 = Triple Axis Accelerometer Breakout - ADXL335

nets:
  N1: 元件1.A3, 元件2.ZOUT
  N2: 元件1.A4/SDA, 元件2.YOUT
  N3: 元件1.A5/SCL, 元件2.XOUT
  3V3: 元件1.3V3, 元件2.VCC
  GND: 元件1.GND, 元件2.GND

// code stored in the sketch: GY-61 ADXL33.ino

const int xPin = A5;
const int yPin = A4;
const int zPin = A3;
//The minimum and maximum values that came from
//the accelerometer while standing still
//You very well may need to change these
int minVal = 265;
int maxVal = 402;


//to hold the caculated values
double x;
double y;
double z;


void setup(){
  Serial.begin(9600); 
}


void loop(){

  //read the analog values from the accelerometer
  int xRead = analogRead(xPin);
  int yRead = analogRead(yPin);
  int zRead = analogRead(zPin);

  //convert read values to degrees -90 to 90 - Needed for atan2
  int xAng = map(xRead, minVal, maxVal, -90, 90);
  int yAng = map(yRead, minVal, maxVal, -90, 90);
  int zAng = map(zRead, minVal, maxVal, -90, 90);

  //Caculate 360deg values like so: atan2(-yAng, -zAng)
  //atan2 outputs the value of -? to ? (radians)
  //We are then converting the radians to degrees
  x = RAD_TO_DEG * (atan2(-yAng, -zAng) + PI);
  y = RAD_TO_DEG * (atan2(-xAng, -zAng) + PI);
  z = RAD_TO_DEG * (atan2(-yAng, -xAng) + PI);

  //Output the caculations
  Serial.print("x: ");
  Serial.print(x);
  Serial.print(" | y: ");
  Serial.print(y);
  Serial.print(" | z: ");
  Serial.println(z);

  delay(100);//just here to slow down the serial output - Easier to read
}
