# Fritzing sketch HC-SR04 (saved by Fritzing 0.9.3b)

parts:
  hc-sr1 = hc-sr04
  元件1 = Arduino Mega 2560 (Rev3)
  D1 = LTE-302 [package=lte-302]

nets:
  VCC: hc-sr1.VCC, 元件1.5V
  N1: hc-sr1.Trig, hc-sr1.Echo, 元件1.D30, 元件1.D31
  GND: hc-sr1.GND, 元件1.GND, D1.C
  N2: 元件1.D13_PWM, D1.A

// code stored in the sketch: hc-sr04.ino
// Trig?Arduino??Digital 5???????Echo?Digital 4?????????

int inputPin = 31; // ???????????
int outputPin = 30; // ???????????
int ledpin = 13;
void setup()
{
  Serial.begin(9600);
  pinMode(ledpin, OUTPUT);
  pinMode(inputPin, INPUT);
  pinMode(outputPin, OUTPUT);
}
void loop()

{
  digitalWrite(outputPin, LOW); // ???????????????2?s
  delayMicroseconds(2);
  digitalWrite(outputPin, HIGH); // ???????????????10?s??????10?s
  delayMicroseconds(10);
  digitalWrite(outputPin, LOW); // ??????????????
  double distance = pulseIn(inputPin, HIGH); // ??????
  distance = distance / 58.0; // ?????????????????
  Serial.println(distance); //?????
  delay(50);
  if (distance >= 50)
  { //??????50??????
    digitalWrite(ledpin, HIGH);
  }//??????50??????
  else
    digitalWrite(ledpin, LOW);
}
